// Digital circuit 1 bit Comparator.dig as structural Verilog
module _1_bit_Comparator (
  input  A,
  input  B,
  output A_lt_B,
  output A_gt_B,
  output A_eq_B
);

  wire not_1_out, not_2_out;

  not not_1 (not_1_out, A);
  not not_2 (not_2_out, B);
  and and_1 (A_lt_B, not_1_out, B);
  and and_2 (A_gt_B, A, not_2_out);
  nor nor_1 (A_eq_B, A_lt_B, A_gt_B);
endmodule
