// Digital circuit 8 bit adder.dig as structural Verilog
module _8_bit_adder (
  input  SU,
  input  [7:0] A,
  input  [7:0] B,
  output OVF,
  output [7:0] S
);

  wire full_adder_1_cout, full_adder_2_cout, full_adder_3_cout, full_adder_4_cout, full_adder_5_cout,
       full_adder_6_cout, full_adder_7_cout, xor_1_out, xor_2_out, xor_3_out, xor_4_out, xor_5_out,
       xor_6_out, xor_7_out, xor_8_out;

  xor xor_1 (xor_1_out, B[0], SU);
  xor xor_2 (xor_2_out, B[1], SU);
  Full_Adder full_adder_1 (.A(A[0]), .B(xor_1_out), .Cin(SU), .S(S[0]), .Cout(full_adder_1_cout));
  xor xor_3 (xor_3_out, B[2], SU);
  Full_Adder full_adder_2 (.A(A[1]), .B(xor_2_out), .Cin(full_adder_1_cout), .S(S[1]), .Cout(full_adder_2_cout));
  xor xor_4 (xor_4_out, B[3], SU);
  Full_Adder full_adder_3 (.A(A[2]), .B(xor_3_out), .Cin(full_adder_2_cout), .S(S[2]), .Cout(full_adder_3_cout));
  xor xor_5 (xor_5_out, B[4], SU);
  Full_Adder full_adder_4 (.A(A[3]), .B(xor_4_out), .Cin(full_adder_3_cout), .S(S[3]), .Cout(full_adder_4_cout));
  xor xor_6 (xor_6_out, B[5], SU);
  Full_Adder full_adder_5 (.A(A[4]), .B(xor_5_out), .Cin(full_adder_4_cout), .S(S[4]), .Cout(full_adder_5_cout));
  xor xor_7 (xor_7_out, B[6], SU);
  Full_Adder full_adder_6 (.A(A[5]), .B(xor_6_out), .Cin(full_adder_5_cout), .S(S[5]), .Cout(full_adder_6_cout));
  xor xor_8 (xor_8_out, B[7], SU);
  Full_Adder full_adder_7 (.A(A[6]), .B(xor_7_out), .Cin(full_adder_6_cout), .S(S[6]), .Cout(full_adder_7_cout));
  Full_Adder full_adder_8 (.A(A[7]), .B(xor_8_out), .Cin(full_adder_7_cout), .S(S[7]), .Cout(OVF));
endmodule
