// Digital circuit 8 bit comparator.dig as structural Verilog
module _8_bit_comparator (
  input  [7:0] A,
  input  [7:0] B,
  output A_lt_B,
  output A_eq_B,
  output A_gt_B
);

  wire _1_bit_comparator_1_a_eq_b, _1_bit_comparator_1_a_gt_b, _1_bit_comparator_1_a_lt_b,
       _1_bit_comparator_2_a_eq_b, _1_bit_comparator_2_a_gt_b, _1_bit_comparator_2_a_lt_b,
       _1_bit_comparator_3_a_eq_b, _1_bit_comparator_3_a_gt_b, _1_bit_comparator_3_a_lt_b,
       _1_bit_comparator_4_a_eq_b, _1_bit_comparator_4_a_gt_b, _1_bit_comparator_4_a_lt_b,
       _1_bit_comparator_5_a_eq_b, _1_bit_comparator_5_a_gt_b, _1_bit_comparator_5_a_lt_b,
       _1_bit_comparator_6_a_eq_b, _1_bit_comparator_6_a_gt_b, _1_bit_comparator_6_a_lt_b,
       _1_bit_comparator_7_a_eq_b, _1_bit_comparator_7_a_gt_b, _1_bit_comparator_7_a_lt_b,
       _1_bit_comparator_8_a_eq_b, _1_bit_comparator_8_a_gt_b, _1_bit_comparator_8_a_lt_b, and_2_out,
       and_3_out, and_4_out, and_5_out, and_6_out, and_7_out, and_8_out, and_9_out, and_10_out, and_11_out,
       and_12_out, and_13_out, and_14_out, and_15_out;

  _1_bit_Comparator _1_bit_comparator_1 (
    .A(A[7]), .B(B[7]), .A_lt_B(_1_bit_comparator_1_a_lt_b), .A_gt_B(_1_bit_comparator_1_a_gt_b),
    .A_eq_B(_1_bit_comparator_1_a_eq_b));
  _1_bit_Comparator _1_bit_comparator_2 (
    .A(A[6]), .B(B[6]), .A_lt_B(_1_bit_comparator_2_a_lt_b), .A_gt_B(_1_bit_comparator_2_a_gt_b),
    .A_eq_B(_1_bit_comparator_2_a_eq_b));
  _1_bit_Comparator _1_bit_comparator_3 (
    .A(A[5]), .B(B[5]), .A_lt_B(_1_bit_comparator_3_a_lt_b), .A_gt_B(_1_bit_comparator_3_a_gt_b),
    .A_eq_B(_1_bit_comparator_3_a_eq_b));
  _1_bit_Comparator _1_bit_comparator_4 (
    .A(A[4]), .B(B[4]), .A_lt_B(_1_bit_comparator_4_a_lt_b), .A_gt_B(_1_bit_comparator_4_a_gt_b),
    .A_eq_B(_1_bit_comparator_4_a_eq_b));
  _1_bit_Comparator _1_bit_comparator_5 (
    .A(A[3]), .B(B[3]), .A_lt_B(_1_bit_comparator_5_a_lt_b), .A_gt_B(_1_bit_comparator_5_a_gt_b),
    .A_eq_B(_1_bit_comparator_5_a_eq_b));
  _1_bit_Comparator _1_bit_comparator_6 (
    .A(A[2]), .B(B[2]), .A_lt_B(_1_bit_comparator_6_a_lt_b), .A_gt_B(_1_bit_comparator_6_a_gt_b),
    .A_eq_B(_1_bit_comparator_6_a_eq_b));
  _1_bit_Comparator _1_bit_comparator_7 (
    .A(A[1]), .B(B[1]), .A_lt_B(_1_bit_comparator_7_a_lt_b), .A_gt_B(_1_bit_comparator_7_a_gt_b),
    .A_eq_B(_1_bit_comparator_7_a_eq_b));
  _1_bit_Comparator _1_bit_comparator_8 (
    .A(A[0]), .B(B[0]), .A_lt_B(_1_bit_comparator_8_a_lt_b), .A_gt_B(_1_bit_comparator_8_a_gt_b),
    .A_eq_B(_1_bit_comparator_8_a_eq_b));
  and and_1 (A_eq_B, _1_bit_comparator_1_a_eq_b, _1_bit_comparator_2_a_eq_b, _1_bit_comparator_3_a_eq_b, _1_bit_comparator_4_a_eq_b, _1_bit_comparator_5_a_eq_b, _1_bit_comparator_6_a_eq_b, _1_bit_comparator_7_a_eq_b, _1_bit_comparator_8_a_eq_b);
  and and_2 (and_2_out, _1_bit_comparator_8_a_gt_b, _1_bit_comparator_7_a_eq_b, _1_bit_comparator_6_a_eq_b, _1_bit_comparator_5_a_eq_b, _1_bit_comparator_4_a_eq_b, _1_bit_comparator_3_a_eq_b, _1_bit_comparator_2_a_eq_b, _1_bit_comparator_1_a_eq_b);
  and and_3 (and_3_out, _1_bit_comparator_7_a_gt_b, _1_bit_comparator_6_a_eq_b, _1_bit_comparator_5_a_eq_b, _1_bit_comparator_4_a_eq_b, _1_bit_comparator_3_a_eq_b, _1_bit_comparator_2_a_eq_b, _1_bit_comparator_1_a_eq_b);
  and and_4 (and_4_out, _1_bit_comparator_6_a_gt_b, _1_bit_comparator_5_a_eq_b, _1_bit_comparator_4_a_eq_b, _1_bit_comparator_3_a_eq_b, _1_bit_comparator_2_a_eq_b, _1_bit_comparator_1_a_eq_b);
  and and_5 (and_5_out, _1_bit_comparator_5_a_gt_b, _1_bit_comparator_4_a_eq_b, _1_bit_comparator_3_a_eq_b, _1_bit_comparator_2_a_eq_b, _1_bit_comparator_1_a_eq_b);
  and and_6 (and_6_out, _1_bit_comparator_4_a_gt_b, _1_bit_comparator_3_a_eq_b, _1_bit_comparator_2_a_eq_b, _1_bit_comparator_1_a_eq_b);
  and and_7 (and_7_out, _1_bit_comparator_3_a_gt_b, _1_bit_comparator_2_a_eq_b, _1_bit_comparator_1_a_eq_b);
  and and_8 (and_8_out, _1_bit_comparator_2_a_gt_b, _1_bit_comparator_1_a_eq_b);
  and and_9 (and_9_out, _1_bit_comparator_1_a_eq_b, _1_bit_comparator_2_a_lt_b);
  and and_10 (and_10_out, _1_bit_comparator_1_a_eq_b, _1_bit_comparator_2_a_eq_b, _1_bit_comparator_3_a_lt_b);
  and and_11 (and_11_out, _1_bit_comparator_1_a_eq_b, _1_bit_comparator_2_a_eq_b, _1_bit_comparator_3_a_eq_b, _1_bit_comparator_4_a_lt_b);
  and and_12 (and_12_out, _1_bit_comparator_1_a_eq_b, _1_bit_comparator_2_a_eq_b, _1_bit_comparator_3_a_eq_b, _1_bit_comparator_4_a_eq_b, _1_bit_comparator_5_a_lt_b);
  and and_13 (and_13_out, _1_bit_comparator_1_a_eq_b, _1_bit_comparator_2_a_eq_b, _1_bit_comparator_3_a_eq_b, _1_bit_comparator_4_a_eq_b, _1_bit_comparator_5_a_eq_b, _1_bit_comparator_6_a_lt_b);
  and and_14 (and_14_out, _1_bit_comparator_1_a_eq_b, _1_bit_comparator_2_a_eq_b, _1_bit_comparator_3_a_eq_b, _1_bit_comparator_4_a_eq_b, _1_bit_comparator_5_a_eq_b, _1_bit_comparator_6_a_eq_b, _1_bit_comparator_7_a_lt_b);
  and and_15 (and_15_out, _1_bit_comparator_1_a_eq_b, _1_bit_comparator_2_a_eq_b, _1_bit_comparator_3_a_eq_b, _1_bit_comparator_4_a_eq_b, _1_bit_comparator_5_a_eq_b, _1_bit_comparator_6_a_eq_b, _1_bit_comparator_7_a_eq_b, _1_bit_comparator_8_a_lt_b);
  xor xor_1 (A_gt_B, and_2_out, and_3_out, and_4_out, and_5_out, and_6_out, and_7_out, and_8_out, _1_bit_comparator_1_a_gt_b);
  xor xor_2 (A_lt_B, _1_bit_comparator_1_a_lt_b, and_9_out, and_10_out, and_11_out, and_12_out, and_13_out, and_14_out, and_15_out);
endmodule
