// Digital circuit ALU.dig as structural Verilog
module ALU (
  input  [7:0] A,
  input  [7:0] B,
  input  [2:0] OPCODE,
  input  L_R,
  output Overflow___2_s_complement
);

  wire _8_bit_comparator_1_a_eq_b, _8_bit_comparator_1_a_gt_b, _8_bit_comparator_1_a_lt_b,
       notconnected_1_out, notconnected_2_out, opcode_selector_1_comp, opcode_selector_1_mult,
       opcode_selector_1_shift, opcode_selector_1_sub, opcode_selector_1_sum;
  wire [7:0] _8_bit_adder_1_s, and_1_out, and_2_out, and_3_out, and_4_out, and_5_out, barrel_shifter_1_o,
       bitextender_1_out, bitextender_2_out, bitextender_3_out, bitextender_4_out, bitextender_5_out,
       comp_handler_1_o, multiplier_1_m, or_1_out;

  _8_bit_adder _8_bit_adder_1 (
    .SU(opcode_selector_1_sub), .A(A), .B(B), .OVF(Overflow___2_s_complement), .S(_8_bit_adder_1_s));
  _8_bit_comparator _8_bit_comparator_1 (
    .A(A), .B(B), .A_lt_B(_8_bit_comparator_1_a_lt_b), .A_eq_B(_8_bit_comparator_1_a_eq_b),
    .A_gt_B(_8_bit_comparator_1_a_gt_b));
  Barrel_Shifter barrel_shifter_1 (.A(A), .L_R(L_R), .O(barrel_shifter_1_o));
  Multiplier multiplier_1 (.A(A), .B(B), .M(multiplier_1_m));
  OPCode_Selector opcode_selector_1 (
    .In(OPCODE), .SUM(opcode_selector_1_sum), .SUB(opcode_selector_1_sub), .COMP(opcode_selector_1_comp),
    .SHIFT(opcode_selector_1_shift), .MULT(opcode_selector_1_mult));
  Comp_Handler comp_handler_1 (
    .A_lt_B(_8_bit_comparator_1_a_lt_b), .A_eq_B(_8_bit_comparator_1_a_eq_b),
    .A_gt_B(_8_bit_comparator_1_a_gt_b), .O(comp_handler_1_o));
  BitExtender #(.inputBits(1), .outputBits(8)) bitextender_1 (.in(opcode_selector_1_sum), .out(bitextender_1_out));
  BitExtender #(.inputBits(1), .outputBits(8)) bitextender_2 (.in(opcode_selector_1_sub), .out(bitextender_2_out));
  BitExtender #(.inputBits(1), .outputBits(8)) bitextender_3 (.in(opcode_selector_1_comp), .out(bitextender_3_out));
  BitExtender #(.inputBits(1), .outputBits(8)) bitextender_4 (.in(opcode_selector_1_shift), .out(bitextender_4_out));
  BitExtender #(.inputBits(1), .outputBits(8)) bitextender_5 (.in(opcode_selector_1_mult), .out(bitextender_5_out));
  assign and_1_out = _8_bit_adder_1_s & bitextender_1_out;  // And and_1, 8 bits wide
  assign and_2_out = _8_bit_adder_1_s & bitextender_2_out;  // And and_2, 8 bits wide
  assign and_3_out = comp_handler_1_o & bitextender_3_out;  // And and_3, 8 bits wide
  assign and_4_out = barrel_shifter_1_o & bitextender_4_out;  // And and_4, 8 bits wide
  assign and_5_out = multiplier_1_m & bitextender_5_out;  // And and_5, 8 bits wide
  assign or_1_out = and_1_out | and_2_out | and_3_out | and_4_out | and_5_out;  // Or or_1, 8 bits wide
  Seven_Seg_Hex seven_seg_hex_1 (.d(or_1_out[7:4]), .dp(notconnected_1_out));
  Seven_Seg_Hex seven_seg_hex_2 (.d(or_1_out[3:0]), .dp(notconnected_2_out));
  // NotConnected on notconnected_1_out
  // NotConnected on notconnected_2_out
endmodule
