// Digital circuit Barrel Shifter.dig as structural Verilog
module Barrel_Shifter (
  input  [7:0] A,
  input  L_R,
  output [7:0] O
);

  wire demultiplexer_1_out_0, demultiplexer_1_out_1;
  wire [7:0] _8_bit_left_shift_1_p5, _8_bit_right_shifter_1_p5;

  Demultiplexer demultiplexer_1 (.sel(L_R), .in(1'b1), .out_0(demultiplexer_1_out_0), .out_1(demultiplexer_1_out_1));
  // _8_bit_left_shift _8_bit_left_shift_1: pin names not known; wires that end beside it: A, demultiplexer_1_out_0, 1'b0, 1'b0, _8_bit_left_shift_1_p5
  // _8_bit_right_shifter _8_bit_right_shifter_1: pin names not known; wires that end beside it: A, demultiplexer_1_out_1, 1'b0, 1'b0, _8_bit_right_shifter_1_p5
  Multiplexer #(.Bits(8)) multiplexer_1 (
    .sel(L_R), .in_0(_8_bit_left_shift_1_p5), .in_1(_8_bit_right_shifter_1_p5), .out(O));
endmodule
