// Digital circuit Comp Handler.dig as structural Verilog
module Comp_Handler (
  input  A_lt_B,
  input  A_eq_B,
  input  A_gt_B,
  output [7:0] O
);

  wire [7:0] and_1_out, and_2_out, and_3_out, bitextender_1_out, bitextender_2_out, bitextender_3_out;

  BitExtender #(.inputBits(1), .outputBits(8)) bitextender_1 (.in(A_lt_B), .out(bitextender_1_out));
  BitExtender #(.inputBits(1), .outputBits(8)) bitextender_2 (.in(A_eq_B), .out(bitextender_2_out));
  BitExtender #(.inputBits(1), .outputBits(8)) bitextender_3 (.in(A_gt_B), .out(bitextender_3_out));
  assign and_1_out = 8'hb & bitextender_1_out;  // And and_1, 8 bits wide
  assign and_2_out = 8'he & bitextender_2_out;  // And and_2, 8 bits wide
  assign and_3_out = 8'ha & bitextender_3_out;  // And and_3, 8 bits wide
  assign O = and_1_out | and_2_out | and_3_out;  // Or or_1, 8 bits wide
endmodule
