// Digital circuit Multiplier.dig as structural Verilog
module Multiplier (
  input  [7:0] A,
  input  [7:0] B,
  output [7:0] M
);

  wire [7:0] _8_bit_adder_1_s, _8_bit_adder_2_s, _8_bit_adder_3_s, _8_bit_adder_4_s, _8_bit_adder_5_s,
       _8_bit_adder_6_s, barrel_shifter_1_o, barrel_shifter_2_o, barrel_shifter_3_o, barrel_shifter_4_o,
       barrel_shifter_5_o, barrel_shifter_6_o, barrel_shifter_7_o, barrel_shifter_8_o, barrel_shifter_9_o,
       barrel_shifter_10_o, barrel_shifter_11_o, barrel_shifter_12_o, barrel_shifter_13_o,
       barrel_shifter_14_o, barrel_shifter_15_o, barrel_shifter_16_o, barrel_shifter_17_o,
       barrel_shifter_18_o, barrel_shifter_19_o, barrel_shifter_20_o, barrel_shifter_21_o,
       barrel_shifter_22_o, barrel_shifter_23_o, barrel_shifter_24_o, barrel_shifter_25_o,
       barrel_shifter_26_o, barrel_shifter_27_o, barrel_shifter_28_o, chooser_1_a0, chooser_1_a1,
       chooser_1_a2, chooser_1_a3, chooser_1_a4, chooser_1_a5, chooser_1_a6, chooser_1_a7;

  Chooser chooser_1 (
    .A(A), .B(B), .A0(chooser_1_a0), .A1(chooser_1_a1), .A2(chooser_1_a2), .A3(chooser_1_a3),
    .A4(chooser_1_a4), .A5(chooser_1_a5), .A6(chooser_1_a6), .A7(chooser_1_a7));
  Barrel_Shifter barrel_shifter_1 (.A(chooser_1_a1), .L_R(1'b0), .O(barrel_shifter_1_o));
  Barrel_Shifter barrel_shifter_2 (.A(chooser_1_a2), .L_R(1'b0), .O(barrel_shifter_2_o));
  Barrel_Shifter barrel_shifter_3 (.A(chooser_1_a3), .L_R(1'b0), .O(barrel_shifter_3_o));
  Barrel_Shifter barrel_shifter_4 (.A(chooser_1_a4), .L_R(1'b0), .O(barrel_shifter_4_o));
  Barrel_Shifter barrel_shifter_5 (.A(chooser_1_a5), .L_R(1'b0), .O(barrel_shifter_5_o));
  Barrel_Shifter barrel_shifter_6 (.A(chooser_1_a6), .L_R(1'b0), .O(barrel_shifter_6_o));
  Barrel_Shifter barrel_shifter_7 (.A(chooser_1_a7), .L_R(1'b0), .O(barrel_shifter_7_o));
  _8_bit_adder _8_bit_adder_1 (.SU(1'b0), .A(chooser_1_a0), .B(barrel_shifter_1_o), .S(_8_bit_adder_1_s));  // open: OVF
  Barrel_Shifter barrel_shifter_8 (.A(barrel_shifter_2_o), .L_R(1'b0), .O(barrel_shifter_8_o));
  Barrel_Shifter barrel_shifter_9 (.A(barrel_shifter_3_o), .L_R(1'b0), .O(barrel_shifter_9_o));
  Barrel_Shifter barrel_shifter_10 (.A(barrel_shifter_4_o), .L_R(1'b0), .O(barrel_shifter_10_o));
  Barrel_Shifter barrel_shifter_11 (.A(barrel_shifter_5_o), .L_R(1'b0), .O(barrel_shifter_11_o));
  Barrel_Shifter barrel_shifter_12 (.A(barrel_shifter_6_o), .L_R(1'b0), .O(barrel_shifter_12_o));
  Barrel_Shifter barrel_shifter_13 (.A(barrel_shifter_7_o), .L_R(1'b0), .O(barrel_shifter_13_o));
  Barrel_Shifter barrel_shifter_14 (.A(barrel_shifter_9_o), .L_R(1'b0), .O(barrel_shifter_14_o));
  Barrel_Shifter barrel_shifter_15 (.A(barrel_shifter_10_o), .L_R(1'b0), .O(barrel_shifter_15_o));
  Barrel_Shifter barrel_shifter_16 (.A(barrel_shifter_11_o), .L_R(1'b0), .O(barrel_shifter_16_o));
  Barrel_Shifter barrel_shifter_17 (.A(barrel_shifter_12_o), .L_R(1'b0), .O(barrel_shifter_17_o));
  Barrel_Shifter barrel_shifter_18 (.A(barrel_shifter_13_o), .L_R(1'b0), .O(barrel_shifter_18_o));
  _8_bit_adder _8_bit_adder_2 (
    .SU(1'b0), .A(barrel_shifter_8_o), .B(barrel_shifter_14_o), .S(_8_bit_adder_2_s));  // open: OVF
  Barrel_Shifter barrel_shifter_19 (.A(barrel_shifter_15_o), .L_R(1'b0), .O(barrel_shifter_19_o));
  Barrel_Shifter barrel_shifter_20 (.A(barrel_shifter_16_o), .L_R(1'b0), .O(barrel_shifter_20_o));
  Barrel_Shifter barrel_shifter_21 (.A(barrel_shifter_17_o), .L_R(1'b0), .O(barrel_shifter_21_o));
  Barrel_Shifter barrel_shifter_22 (.A(barrel_shifter_18_o), .L_R(1'b0), .O(barrel_shifter_22_o));
  _8_bit_adder _8_bit_adder_3 (
    .SU(1'b0), .A(_8_bit_adder_1_s), .B(_8_bit_adder_2_s), .S(_8_bit_adder_3_s));  // open: OVF
  Barrel_Shifter barrel_shifter_23 (.A(barrel_shifter_20_o), .L_R(1'b0), .O(barrel_shifter_23_o));
  Barrel_Shifter barrel_shifter_24 (.A(barrel_shifter_21_o), .L_R(1'b0), .O(barrel_shifter_24_o));
  Barrel_Shifter barrel_shifter_25 (.A(barrel_shifter_22_o), .L_R(1'b0), .O(barrel_shifter_25_o));
  _8_bit_adder _8_bit_adder_4 (
    .SU(1'b0), .A(barrel_shifter_19_o), .B(barrel_shifter_23_o), .S(_8_bit_adder_4_s));  // open: OVF
  Barrel_Shifter barrel_shifter_26 (.A(barrel_shifter_24_o), .L_R(1'b0), .O(barrel_shifter_26_o));
  Barrel_Shifter barrel_shifter_27 (.A(barrel_shifter_25_o), .L_R(1'b0), .O(barrel_shifter_27_o));
  Barrel_Shifter barrel_shifter_28 (.A(barrel_shifter_27_o), .L_R(1'b0), .O(barrel_shifter_28_o));
  _8_bit_adder _8_bit_adder_5 (
    .SU(1'b0), .A(barrel_shifter_26_o), .B(barrel_shifter_28_o), .S(_8_bit_adder_5_s));  // open: OVF
  _8_bit_adder _8_bit_adder_6 (
    .SU(1'b0), .A(_8_bit_adder_4_s), .B(_8_bit_adder_5_s), .S(_8_bit_adder_6_s));  // open: OVF
  _8_bit_adder _8_bit_adder_7 (.SU(1'b0), .A(_8_bit_adder_3_s), .B(_8_bit_adder_6_s), .S(M));  // open: OVF
endmodule
