// Digital circuit OPCode Selector.dig as structural Verilog
module OPCode_Selector (
  input  [2:0] In,
  output SUM,
  output SUB,
  output COMP,
  output SHIFT,
  output MULT
);

  wire not_1_out, not_2_out, not_3_out;

  not not_1 (not_1_out, In[0]);
  not not_2 (not_2_out, In[1]);
  not not_3 (not_3_out, In[2]);
  and and_1 (SUM, In[0], not_2_out, not_3_out);
  and and_2 (SUB, not_1_out, In[1], not_3_out);
  and and_3 (COMP, In[0], In[1], not_3_out);
  and and_4 (SHIFT, not_1_out, not_2_out, In[2]);
  and and_5 (MULT, In[0], not_2_out, In[2]);
endmodule
